# Fritzing sketch Plant-Protector (saved by Fritzing 0.9.3b)

parts:
  R1 = BBC MicroBit
  Part1 = Soil Moisture Sensor
  SP1 = SPEAKER [package=pcb_mount_speaker]

nets:
  GND: R1.GND, Part1.GND, SP1.+
  3V3: R1.3v3, Part1.VCC
  N1: R1.P1_ANALOG_IN, Part1.SIG
  N2: R1.P0_ANALOG_IN, SP1.-

custom parts:
  BBC MicroBit: The BBC MICRO:BIT
